// Logisim project proyecto.circ as structural Verilog: 1 circuit, main circuit main
module main (
  input  A,
  input  B,
  input  C,
  input  D,
  input  in_5,
  input  E,
  input  in_7,
  input  in_8,
  input  in_9,
  input  _257,
  input  _258,
  input  in_12,
  input  _259,
  input  in_14,
  input  _261,
  input  in_16,
  input  _262,
  input  in_18,
  input  in_19,
  input  in_20
);

  wire clock_1_out, multiplexer_1_out;
  wire [3:0] counter_1_q, multiplexer_2_out;
  wire [3:3] or_1_out;
  wire [8:0] multiplexer_3_out;

  or or_1 (or_1_out[3], A, B, C, D, E);
  ROM rom_1 ();  // open: addr, data
  Multiplexer #(.select(3)) multiplexer_1 (
    .in0(_257), .in1(_258), .in2(_259), .in3(_261), .in4(_262), .in5(in_19), .out(multiplexer_1_out),
    .sel(multiplexer_3_out[2:0]));  // open: in6, in7
  Multiplexer #(.select(4), .width(4)) multiplexer_2 (
    .out(multiplexer_2_out), .sel({or_1_out[3], multiplexer_3_out[2:0]}));  // open: in0, in1, in2, in3, in4, in5, in6, in7, in8, in9, in10, in11, in12, in13, in14, in15
  Clock clock_1 (.out(clock_1_out));
  Counter #(.max('hf), .width(4)) counter_1 (
    .up(1'b1), .count(multiplexer_1_out), .clk(clock_1_out), .D(multiplexer_2_out), .Q(counter_1_q));  // open: clr, load, carry
  Multiplexer #(.select(4), .width(9)) multiplexer_3 (
    .in1(9'h100), .in2(9'h101), .in3(9'h102), .in4(9'h103), .in5(9'h104), .in6(9'h105), .in7(9'h106),
    .out(multiplexer_3_out), .sel(counter_1_q));  // open: in0, in8, in9, in10, in11, in12, in13, in14, in15

  // Notes on the sheet:
  //   260
endmodule
